# Fritzing sketch lapcounter (saved by Fritzing 0.9.10b)
circuit board: 6.19984cm x 4.62941cm

parts:
  Part1 = Arduino Nano (Rev3.0)
  Buzz = Active Buzzer
  R1 = Trimmer Potentiometer [maximum_resistance=1kΩ knob_status=50% power=0.5W package=THT]
  J2 = MH-ET e-ink [package=THT]
  R2 = Trimmer Potentiometer [maximum_resistance=100kΩ knob_status=50% power=0.5W package=THT]
  R3 = Resistor [tolerance=±5% power=0.25 resistance=330k package=THT]
  LED1 = LED - 5mm [color="Red (633nm)" current=10mA package="5 mm [THT]"]
  CHECK = female pin header, 1 pin [form="♀ (female)"]
  C1 = Ceramic Capacitor [capacitance=100pF voltage=35V package="100 mil [THT, multilayer]"]
  MODES = DIP SWITCH [package=dipswitch-02]
  GND = female pin header, 1 pin [form="♀ (female)"]
  CAP = female pin header, 1 pin [form="♀ (female)"]
  S2 = Round Pushbutton
  R32 = Trimmer Potentiometer [maximum_resistance=1MΩ knob_status=50% power=0.5W package=THT]
  SW5 = DIP SWITCH [package=dipswitch-02]
  SW4 = DIP SWITCH [package=dipswitch-02]
  R22 = Resistor [tolerance=±5% power=0.25 resistance=22M package=THT]
  R25 = Resistor [tolerance=±5% resistance=3.3M power=0.25 package="0805 [SMD]"]
  R24 = Resistor [tolerance=±5% resistance=4.7M power=0.25 package="0805 [SMD]"]
  R21 = Resistor [tolerance=±5% resistance=10M power=0.25 package="0805 [SMD]"]
  R6 = Resistor [tolerance=±5% power=0.25 resistance=1k package=THT]
  R33 = Resistor [tolerance=±5% power=0.25 resistance=22M package=THT]
  R4 = Resistor [tolerance=±5% power=0.25 resistance=100k package=THT]
  R34 = Trimmer Potentiometer [maximum_resistance=1kΩ knob_status=50% power=0.5W package=THT]

nets:
  GND: Part1.GND, Buzz.-, J2.GND, R2.leg1, C1.0, MODES.1, MODES.2, GND.pin1, R34.leg2
  N1: Part1.D4, Buzz.Signal
  N2: Part1.D5, R3.Pin_0
  N3: Part1.D7, J2.Busy
  N4: Part1.D8, J2.Reset
  N5: Part1.D9, J2.DC
  N6: Part1.D10, J2.CS
  N7: Part1.D11/MOSI, J2.SDI
  5V: Part1.5V, R1.wiper, J2.VCC, R2.leg2
  N8: Part1.A4, R2.wiper
  N9: Part1.A3, R4.Pin_0
  N10: Part1.A2, R6.Pin_0
  N11: Part1.A1, MODES.4
  N12: Part1.A0, MODES.3
  N13: Part1.D13/SCK, J2.SCLK
  N14: Buzz.VCC, R1.leg1
  N15: R3.Pin_1, LED1.anode
  N16: LED1.cathode, R34.wiper
  N17: CHECK.pin1, SW4.4, R25.Pin_0, R4.Pin_1
  N18: C1.1, CAP.pin1, R32.wiper, R6.Pin_1
  N19: S2.leg0, SW5.3, R22.Pin_1, R33.Pin_0
  N20: S2.leg1, R32.leg1, R33.Pin_1
  N21: SW5.1, SW5.2, R22.Pin_0, R21.Pin_1
  N22: SW5.4, SW4.3, R24.Pin_1, R21.Pin_0
  N23: SW4.1, SW4.2, R25.Pin_1, R24.Pin_0

custom parts:
  Active Buzzer: Active Buzzer, GND, Signal, VCC.
