# Fritzing sketch pot (saved by Fritzing 0.9.10b)
breadboards: 1

parts:
  R1 = Resistor [tolerance=±5% power=0.25 resistance=22M package=THT]
  R9 = Resistor [tolerance=±5% power=0.25 resistance=22M package=THT]
  R10 = Resistor [tolerance=±5% power=0.25 resistance=22M package=THT]
  R11 = Resistor [tolerance=±5% power=0.25 resistance=22M package=THT]
  R12 = Resistor [tolerance=±5% power=0.25 resistance=22M package=THT]
  R13 = Resistor [tolerance=±5% power=0.25 resistance=22M package=THT]
  R14 = Resistor [tolerance=±5% power=0.25 resistance=22M package=THT]
  R15 = Resistor [tolerance=±5% power=0.25 resistance=22M package=THT]
  R16 = Trimmer Potentiometer [maximum_resistance=1MΩ knob_status=50% power=0.5W package=THT]
  SW2 = DIP SWITCH [package=dipswitch-02]
  R17 = Resistor [tolerance=±5% power=0.25 resistance=100k package=THT]
  SW3 = DIP SWITCH [package=dipswitch-02]
  J1 = female pin header, 1 pin [form="♀ (female)"]
  J2 = female pin header, 1 pin [form="♀ (female)"]
  S1 = Round Pushbutton
  R18 = Resistor [tolerance=±5% power=0.25 resistance=1M package=THT]
  R19 = Resistor [tolerance=±5% power=0.25 resistance=1M package=THT]
  R20 = Resistor [tolerance=±5% power=0.25 resistance=1M package=THT]

nets:
  N1: R1.Pin_0, R9.Pin_0, R10.Pin_0, R11.Pin_0, SW2.4, J1.pin1
  N2: R1.Pin_1, R9.Pin_1, R10.Pin_1, R11.Pin_1, R12.Pin_0, R13.Pin_0, SW2.1, SW2.2
  N3: R12.Pin_1, R13.Pin_1, R15.Pin_0, SW2.3, SW3.4
  N4: R14.Pin_0, R15.Pin_1, SW3.1, SW3.2
  N5: R14.Pin_1, SW3.3, S1.leg0, R20.Pin_0
  N6: R16.leg1, R17.Pin_1
  N7: R16.wiper, S1.leg1, R18.Pin_1
  N8: R17.Pin_0, J2.pin1
  N9: R18.Pin_0, R19.Pin_1
  N10: R19.Pin_0, R20.Pin_1
